# Fritzing sketch RFID_full_setup (saved by Fritzing 0.9.3b)
breadboards: 1

parts:
  Part1 = Arduino Uno (Rev3)
  R1 = Resistor [tolerance=±5% resistance=220 package=THT]
  R2 = Resistor [tolerance=±5% resistance=220 package=THT]
  LED1 = LED - 5mm [color="Red (633nm)" package="5 mm [THT]"]
  LED2 = LED - 5mm [color="Green (570nm)" package="5 mm [THT]"]
  J1 = Piezo Speaker
  Part2 = RFID-RC522-v2

nets:
  N1: Part1.D8, J1.pin1
  N2: Part1.D9_PWM, Part2.RST
  N3: Part1.D10_PWM/SS, Part2.SDA
  N4: Part1.D11_PWM/MOSI, Part2.MOSI
  N5: Part1.D12/MISO, Part2.MISO
  N6: Part1.D13/SCK, Part2.SCK
  GND: Part1.GND, LED1.cathode, LED2.anode, J1.pin2, Part2.GND
  N7: Part1.D6_PWM, R1.Pin_1
  N8: Part1.D7, R2.Pin_0
  3V3: Part1.3V3, Part2.3.3V
  N9: R1.Pin_0, LED1.anode
  N10: R2.Pin_1, LED2.cathode

custom parts:
  RFID-RC522-v2: A simple China made RFID-RC522 Reader; do check the pin labels, as this is a MFRC522 based clone.
